# Fritzing sketch waveglide (saved by Fritzing 0.9.2b)
circuit board: 6.80001cm x 12cm

parts:
  ChargeBooster = PowerBoost 500 Charger
  buzzer = Piezo Speaker
  MXPV7002G = IC, DIP package, 8 pins [chip_label=MXPV7002G]
  OLED1 = 1.27" 128x96 16-bit OLED Breakout  # not connected
  DisplayHeader = female pin header, 11 pins [form="♀ (female)"]
  1uF = Ceramic Capacitor [capacitance=1µF voltage=20V package="100 mil [THT, multilayer]"]
  0_01uF = Ceramic Capacitor [capacitance=0.01µF voltage=20V package="100 mil [THT, multilayer]"]
  470pF = Ceramic Capacitor [capacitance=470pF voltage=20V package="100 mil [THT, multilayer]"]
  EValve1 = female pin header, 1 pin [form="♀ (female)"]
  EValve2 = female pin header, 1 pin [form="♀ (female)"]
  menu_btn = SWITCH-MOMENTARY-2 [package=tactile-pth-12mm]
  EValve = Solenoid
  trinket = Pro Trinket 5V
  ptn1_gnd = female pin header, 1 pin [form="♀ (female)"]
  ptn2_in = female pin header, 1 pin [form="♀ (female)"]
  ptn3_adj = female pin header, 1 pin [form="♀ (female)"]
  ptn4_out = female pin header, 1 pin [form="♀ (female)"]
  SSR = IC, DIP package, 4 pins [chip_label=SSR]
  22uF_(optional) = Ceramic Capacitor [capacitance=22µF package="100 mil [THT, multilayer]"]
  BMP180 = male pin header, 5 pins [form="♂ (male)"]
  360 = Resistor [tolerance=±5% resistance=360 package=THT]
  diode = Rectifier Diode [part_number=1N4001 package="300 mil [THT]"]
  power_btn = SWITCH-MOMENTARY-2 [package=tactile-pth-12mm]
  uart = female pin header, 4 pins [form="♀ (female)"]
  100uF_2 = Electrolytic Capacitor [capacitance=100µF voltage=50V package="200 mil [THT, electrolytic]"]
  100uF_1 = Electrolytic Capacitor [capacitance=100µF voltage=50V package="200 mil [THT, electrolytic]"]
  1_33k = Resistor [tolerance=±5% resistance=1.33k package=THT]
  1_33k_2 = Resistor [tolerance=±5% resistance=1.33k package=THT]

nets:
  N1: ChargeBooster.VBAT, SSR.pin4, 1_33k.Pin_0
  N2: ChargeBooster.ENABLE, power_btn.2
  GND: ChargeBooster.GND, buzzer.pin1, MXPV7002G.pin3, DisplayHeader.pin11, 1uF.0, 0_01uF.0, 470pF.0, EValve1.pin1, menu_btn.1, EValve.pin1, trinket.GND, ptn1_gnd.pin1, SSR.pin2, 22uF_(optional).0, BMP180.pin3, diode.anode, power_btn.1, uart.pin2, 100uF_2.-, 100uF_1.-, 1_33k_2.Pin_1
  N3: ChargeBooster.5.0V, MXPV7002G.pin2, DisplayHeader.pin10, 1uF.1, 0_01uF.1, trinket.+5V, trinket.AREF, BMP180.pin5, uart.pin1
  N4: buzzer.pin2, trinket.D5
  N5: MXPV7002G.pin4, 470pF.1, trinket.A3
  N6: DisplayHeader.pin1, trinket.D11
  N7: DisplayHeader.pin2, trinket.D13
  N8: DisplayHeader.pin3, trinket.D8
  N9: DisplayHeader.pin4, trinket.D9
  N10: DisplayHeader.pin5, trinket.D10
  N11: DisplayHeader.pin6, trinket.D4
  N12: DisplayHeader.pin7, trinket.D12
  N13: EValve2.pin1, EValve.pin2, ptn4_out.pin1, diode.cathode, 100uF_2.+
  N14: menu_btn.2, trinket.D3
  N15: trinket.D6, 360.Pin_0
  N16: trinket.TXD, uart.pin3
  N17: trinket.RXD, uart.pin4
  N18: trinket.A2, 1_33k.Pin_1
  N19: trinket.A4, BMP180.pin1
  N20: trinket.A5, BMP180.pin2
  N21: ptn2_in.pin1, SSR.pin3, 22uF_(optional).1, 100uF_1.+
  N22: ptn3_adj.pin1, 1_33k_2.Pin_0
  N23: SSR.pin1, 360.Pin_1

notes:
  power LED
  low bat LED
  charging LED
  full LED
  12V booster
  O2 IN
  O2 OUT
  WaveGlide
  WaveGlide (beta-02) - Nortd Labs 2015
  BMP180

custom parts:
  PowerBoost 500 Charger: The PowerBoost 500C is a little DC/DC boost converter module that can be powered by any 3.7V LiIon/LiPoly battery, and convert the battery output to 5.2V DC for running your 5V projects. At its heart is a TPS61090 boost converter from TI. This boost converter chip has some really nice extras such as low battery detection, 2A internal switch, synchronous conversion, excellent efficiency, and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
  Pro Trinket 5V: The Pro Trinket 5V is like an Arduino Pro Mini with more pins and USB included. Built with the common core Arduino chip, the ATmega328p, it has 18 GPIO, 2 extra analog inputs, 28K of flash, and 2K of RAM. It has onboard USB bootloading support with Optiboot support, so you can either program your Pro Trinket over USB or with a FTDI cable. The Pro Trinket is programmable using the Arduino IDE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
