# Fritzing sketch waveglide (saved by Fritzing 0.9.2b)

parts:
  ChargeBooster = PowerBoost 500 Charger
  Buzzer_(btm) = Piezo Speaker
  MXPV7002G = IC, DIP package, 8 pins [chip_label=MXPV7002G]
  OLED1 = 1.27" 128x96 16-bit OLED Breakout  # not connected
  DisplayHeader = female pin header, 11 pins [form="♀ (female)"]
  C1 = Ceramic Capacitor [capacitance=1µF voltage=20V package="100 mil [THT, multilayer]"]
  C2 = Ceramic Capacitor [capacitance=0.01µF voltage=20V package="100 mil [THT, multilayer]"]
  C3 = Ceramic Capacitor [capacitance=470pF voltage=20V package="100 mil [THT, multilayer]"]
  EValve1 = female pin header, 1 pin [form="♀ (female)"]
  EValve2 = female pin header, 1 pin [form="♀ (female)"]
  menu_btn = SWITCH-MOMENTARY-2 [package=tactile-pth-12mm]
  EValve = Solenoid
  Trinket = Pro Trinket 5V
  ptn1_gnd = female pin header, 1 pin [form="♀ (female)"]
  ptn2_in = female pin header, 1 pin [form="♀ (female)"]
  ptn3_adj = female pin header, 1 pin [form="♀ (female)"]
  ptn4_out = female pin header, 1 pin [form="♀ (female)"]
  SSR = IC, DIP package, 4 pins [chip_label=SSR]
  C6_(btm) = Ceramic Capacitor [capacitance=22µF package="100 mil [THT, multilayer]"]
  BMP180_(btm) = male pin header, 5 pins [form="♂ (male)"]
  R2 = Resistor [tolerance=±5% resistance=330 package=THT]
  D1 = Rectifier Diode [part_number=1N4001 package="300 mil [THT]"]
  power_btn = SWITCH-MOMENTARY-2 [package=tactile-pth-12mm]
  R5_(btm) = Resistor [tolerance=±5% resistance=1.33k package=THT]
  serial = female pin header, 4 pins [form="♀ (female)"]
  C5_(btm) = Electrolytic Capacitor [capacitance=100µF voltage=50V package="200 mil [THT, electrolytic]"]
  C4_(btm) = Electrolytic Capacitor [capacitance=100µF voltage=50V package="200 mil [THT, electrolytic]"]

nets:
  N1: ChargeBooster.VBAT, Trinket.A2, SSR.pin4
  N2: ChargeBooster.ENABLE, power_btn.2
  GND: ChargeBooster.GND, Buzzer_(btm).pin1, MXPV7002G.pin3, DisplayHeader.pin11, C1.0, C2.0, C3.0, EValve1.pin1, menu_btn.1, EValve.pin1, Trinket.GND, ptn1_gnd.pin1, SSR.pin2, C6_(btm).0, BMP180_(btm).pin3, D1.anode, power_btn.1, R5_(btm).Pin_1, serial.pin2, C5_(btm).-, C4_(btm).-
  N3: ChargeBooster.LBO, Trinket.A1
  N4: ChargeBooster.5.0V, MXPV7002G.pin2, DisplayHeader.pin10, C1.1, C2.1, Trinket.+5V, Trinket.AREF, BMP180_(btm).pin5, serial.pin1
  N5: ChargeBooster.USB, Trinket.A0
  N6: Buzzer_(btm).pin2, Trinket.D5
  N7: MXPV7002G.pin4, C3.1, Trinket.A3
  N8: DisplayHeader.pin1, Trinket.D11
  N9: DisplayHeader.pin2, Trinket.D13
  N10: DisplayHeader.pin3, Trinket.D8
  N11: DisplayHeader.pin4, Trinket.D9
  N12: DisplayHeader.pin5, Trinket.D10
  N13: DisplayHeader.pin6, Trinket.D4
  N14: DisplayHeader.pin7, Trinket.D12
  N15: EValve2.pin1, EValve.pin2, ptn4_out.pin1, D1.cathode, C5_(btm).+
  N16: menu_btn.2, Trinket.D3
  N17: Trinket.D6, R2.Pin_0
  N18: Trinket.TXD, serial.pin3
  N19: Trinket.RXD, serial.pin4
  N20: Trinket.A4, BMP180_(btm).pin1
  N21: Trinket.A5, BMP180_(btm).pin2
  N22: ptn2_in.pin1, SSR.pin3, C6_(btm).1, C4_(btm).+
  N23: ptn3_adj.pin1, R5_(btm).Pin_0
  N24: SSR.pin1, R2.Pin_1

notes:
  power LED
  low bat LED
  charging LED
  full LED
  12V booster
  O2 IN
  O2 OUT
  WaveGlide
  WaveGlide (beta-01) - Nortd Labs 2015
  BMP180

custom parts:
  PowerBoost 500 Charger: The PowerBoost 500C is a little DC/DC boost converter module that can be powered by any 3.7V LiIon/LiPoly battery, and convert the battery output to 5.2V DC for running your 5V projects. At its heart is a TPS61090 boost converter from TI. This boost converter chip has some really nice extras such as low battery detection, 2A internal switch, synchronous conversion, excellent efficiency, and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
  Pro Trinket 5V: The Pro Trinket 5V is like an Arduino Pro Mini with more pins and USB included. Built with the common core Arduino chip, the ATmega328p, it has 18 GPIO, 2 extra analog inputs, 28K of flash, and 2K of RAM. It has onboard USB bootloading support with Optiboot support, so you can either program your Pro Trinket over USB or with a FTDI cable. The Pro Trinket is programmable using the Arduino IDE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
